# Fritzing sketch IRProxy_ESP32-C3 (saved by Fritzing 1.0.5)
breadboards: 1

parts:
  A1 = Esp32-c3 super mini
  LED1 = smd LED [color="Infrared (940nm)" package="0603 [SMD]"]
  LED2 = smd LED [color="Infrared (940nm)" package="0603 [SMD]"]
  R1 = Resistor [tolerance=±0.5% resistance=22 package="1206 [SMD]"]
  R2 = Resistor [tolerance=±5% resistance=220 package="1206 [SMD]"]
  Q1 = MOSFET-NCHANNEL [package=to-92]
  IR1 = TSOP312.., 314.. [package=THT]

nets:
  N1: A1.Pin_6, IR1.Data
  N2: A1.Pin_9, R2.Pin_0
  N3: A1.Pin_14, IR1.Vs
  N4: A1.Pin_15, Q1.D, IR1.GND
  N5: A1.Pin_16, LED1.anode
  N6: LED1.cathode, LED2.anode
  N7: LED2.cathode, R1.Pin_1
  N8: R1.Pin_0, Q1.S
  N9: R2.Pin_1, Q1.G

custom parts:
  Esp32-c3 super mini: ESP32-C3 Development Board ESP32 SuperMini Development Board ESP32 Development Board WiFi Bluetooth.
  MOSFET-NCHANNEL: Generic NMOS footprint
